# Fritzing sketch 461project circuit diagram (saved by Fritzing 1.0.4)
breadboards: 2

parts:
  Part1 = LCD1602-I2C
  Part2 = Arduino Uno (Rev3) - ICSP
  JACK1 = 2.1mm Barrel Jack with Terminal Block
  Entry_Gate = HC-SR04 Ultrasonic Distance Sensor
  Exit_Gate = HC-SR04 Ultrasonic Distance Sensor
  JACK2 = 2.1mm Barrel Jack with Terminal Block
  SLot2 = Tower Pro SG90 servo [part_number=101246]
  SLot1 = Tower Pro SG90 servo [part_number=101246]
  M1 = 1 chan 5v relay module
  Slot3_Dc_Motor = DC Motor [voltage_(max)=6V voltage_(min)=3V]
  M2 = 1 chan 5v relay module
  Q1 = NPN-Transistor [package="TO92 [THT]"]
  L2 = Inductor [package="1206 [SMD]"]
  R1 = Resistor [tolerance=±5% resistance=220 package="0805 [SMD]"]  # not connected
  L3 = Inductor [package="1206 [SMD]"]  # not connected
  L4 = Inductor [package="0805 [SMD]"]  # not connected
  LED1 = smd LED [color="Red (633nm)" package="0603 [SMD]"]  # not connected
  Exit_servo = Tower Pro SG90 servo [part_number=101246]
  ENtry_Servo = Tower Pro SG90 servo [part_number=101246]
  M3 = fc-51 [package=THT]
  M4 = fc-51 [package=THT]
  M5 = fc-51 [package=THT]
  LED2 = smd LED [color="Red (633nm)" package="0603 [SMD]"]
  LED3 = smd LED [color="Red (633nm)" package="0603 [SMD]"]
  LED4 = smd LED [color="Red (633nm)" package="0603 [SMD]"]
  R2 = Resistor [tolerance=±5% resistance=220 package="0805 [SMD]"]
  R3 = Resistor [tolerance=±5% resistance=220 package="0805 [SMD]"]
  R4 = Resistor [tolerance=±5% resistance=220 package="0805 [SMD]"]
  Gizwits_WiFi_Witty_ESP-12F1 = Gizwits WiFi Witty ESP-12F

nets:
  GND: Part1.GND, Part2.GND, JACK1.NEG, M2.pin_2, Q1.B, M3.pin2, M4.pin2, M5.pin2, LED2.cathode, LED3.cathode, LED4.cathode
  N1: Part1.VCC, JACK1.POS, M2.pin_1, M2.pin_5, M5.pin3
  N2: Part1.SDA, Part2.A4/SDA
  N3: Part1.SCL, Part2.A5/SCL
  N4: Part2.A0, R3.Pin_1
  N5: Part2.A1, R4.Pin_1
  N6: Part2.A2, R2.Pin_1
  N7: Part2.A3, M2.pin_3
  N8: Part2.D8, M3.pin1
  N9: Part2.D9_PWM, ENtry_Servo.Signal
  N10: Part2.D10_PWM/SS, Exit_servo.Signal
  N11: Part2.D11_PWM/MOSI, SLot1.Signal
  N12: Part2.D12/MISO, SLot2.Signal
  N13: Part2.D13/SCK, M1.pin_3
  N14: Part2.D0/RX, Gizwits_WiFi_Witty_ESP-12F1.TXD
  N15: Part2.D1/TX, Gizwits_WiFi_Witty_ESP-12F1.RXD
  N16: Part2.D2, Entry_Gate.TRIG
  N17: Part2.D3_PWM, Entry_Gate.ECHO
  N18: Part2.D4, Exit_Gate.TRIG
  N19: Part2.D5_PWM, Exit_Gate.ECHO
  N20: Part2.D6_PWM, M5.pin1
  N21: Part2.D7, M4.pin1
  +5V: Entry_Gate.VCC, Exit_Gate.VCC, JACK2.POS, SLot2.+5V, SLot1.+5V, M1.pin_1, M1.pin_5, Exit_servo.+5V, ENtry_Servo.+5V
  GND_2: Entry_Gate.GND, Exit_Gate.GND, JACK2.NEG, SLot2.GND, SLot1.GND, M1.pin_2, Slot3_Dc_Motor.pin_2, Exit_servo.GND, ENtry_Servo.GND
  N22: M1.pin_6, Slot3_Dc_Motor.pin_1
  N23: M2.pin_6, L2.pin_0
  N24: M3.pin3, M4.pin3
  N25: LED2.anode, R2.Pin_0
  N26: LED3.anode, R3.Pin_0
  N27: LED4.anode, R4.Pin_0

custom parts:
  LCD1602-I2C: A standard character display, usually with 2x16 characters. Comes in many colors with LCM1602 IIC attached.
  Tower Pro SG90 servo: Original file by John De Cristofaro http://www.adafruit.com/products/1449 Adafruit Feedback Servo (Small) Edited by: e-radionica.com 28/9/2015
  1 chan 5v relay module: 1 Channel 5V Relay Module Board Shield with Optocoupler Support High and Low Level Trigger for Arduino.
